# Fritzing sketch GolfHoleCircuit (saved by Fritzing 0.9.3b)
breadboards: 1

parts:
  Part1 = Arduino Uno (Rev3)
  R1 = PHOTOCELL [package=photocell]
  Laser = LD
  LED2 = smd LED [color="Yellow (592nm)" package="0805 [SMD]"]
  LED3 = smd LED [color="Yellow (592nm)" package="0805 [SMD]"]
  Resistor = Resistor [tolerance=±5% resistance=10k package="0402 [SMD]"]
  LED4 = smd LED [color="Blue (525nm)" package="0805 [SMD]"]
  LED5 = smd LED [color="Blue (525nm)" package="0805 [SMD]"]
  LED6 = smd LED [color="Blue (525nm)" package="0805 [SMD]"]
  J1 = Basic Servo
  LED7 = smd LED [color="Yellow (592nm)" package="0805 [SMD]"]
  PIezo = Piezo Speaker

nets:
  N1: Part1.A0, R1.P$2, Resistor.Pin_0
  N2: Part1.D8, PIezo.pin2
  N3: Part1.D9_PWM, J1.pulse
  GND: Part1.GND, Laser.cathode, LED2.cathode, LED3.cathode, Resistor.Pin_1, LED4.cathode, LED5.cathode, LED6.cathode, J1.gnd, LED7.cathode, PIezo.pin1
  N4: Part1.D2, Laser.anode
  N5: Part1.D3_PWM, LED4.anode, LED5.anode, LED6.anode
  N6: Part1.D4, LED2.anode, LED3.anode, LED7.anode
  5V: Part1.5V, R1.P$1, J1.vcc

custom parts:
  LD: A Generic Red Dot Laser Diode Module (~5mW)

// code stored in the sketch: TripLaser.ino
/* light beam trigger based on SWEEP by Scott Fitzgerald & Barragan and the adafruit photocell
    test

		A laser pointer is used to create a tripwire across a box. When the beam is 
		broken the servo is activated and a flag is raised. Then two rows of leds light up
		in an alternating pattern. A delay of 2 seconds happens and then the whole thing resets. 
		Added a siren sound with a piezo.

		by Matthew K. Bardoe
		July 15, 2016


*/

#include <Servo.h>

Servo myservo;  // create servo object to control a servo

// twelve servo objects can be created on most boards
int laserPin = 2;
int blueLED = 3;
int yellowLED = 4;
// Siren info
int speakerpin = 8; // the pin to which the Piezo will be attached  (other Piezo wire is grounded)
int lowpitch = 500;
int highpitch = 3000;

int servoPosition = 90;
int pos = 90;    // variable to store the servo position
int photocellPin = A0;     // the cell and 10K pulldown are connected to a0
int photocellReading = 0;
int photocellInit = 0;
void setup() {
  Serial.begin(9600);
  myservo.attach(9);  // attaches the servo on pin 9 to the servo object
  // Set the pins
  pinMode(2, OUTPUT);
  pinMode(3, OUTPUT);
  pinMode(4, OUTPUT);
  // test lights
  lightLights();
  // Test laser
  digitalWrite(2, HIGH); //Turn on Laser
  while (photocellInit < 900)
  {
    photocellReading = analogRead(photocellPin);
    photocellInit = 0.1 * photocellReading + .9 * photocellInit;
    Serial.println(photocellReading);
  }
  Serial.println("BEGIN");
  myservo.write(servoPosition);
}

void loop() {
  photocellReading = analogRead(photocellPin);
  if (photocellReading < 950) {
    //Raise
    digitalWrite(laserPin, LOW);
    Serial.println("Raise the flag");
    for (pos = 90; pos <= 172; pos += 10) { // goes from 0 degrees to 180 degrees
      // in steps of 1 degree
      myservo.write(pos);              // tell servo to go to position in variable 'pos'
      delay(15);                       // waits 15ms for the servo to reach the position
    }
    for (int i = 0; i < 3; i++)
    {
      lightLights();
    }
    servoPosition = 172;
    delay(2000);
    digitalWrite(laserPin, HIGH);
    delay(200);
  }
  else if (servoPosition != 90 ) {
    Serial.println("Lower the flag");
    for (pos = 172; pos >= 90; pos -= 1) { // goes from 180 degrees to 0 degrees
      myservo.write(pos);              // tell servo to go to position in variable 'pos'
      delay(15);                       // waits 15ms for the servo to reach the position
    }
    servoPosition = 90;

  }
}

void lightLights() {
  Serial.println("Light Blue lights");
  digitalWrite(3, HIGH);
  
    for (int pitch = lowpitch; pitch < highpitch; pitch++) { // cycles the pitch up from lowpitch to high pitch (Hz)
      tone(speakerpin, pitch, 3);  //plays a given tone for 2ms

    }
    for (int pitch = highpitch; pitch > lowpitch; pitch--) { // cycles the pitch down from higpitch to lowpitch
      // play the tone for 20 ms on pin 8
      tone(speakerpin, pitch, 3);

    }
  
  //delay(500);
  Serial.println("Light Yellow lights");

  digitalWrite(3, LOW);
  digitalWrite(4, HIGH);
  
    for (int pitch = lowpitch; pitch < highpitch; pitch++) { // cycles the pitch up from lowpitch to high pitch (Hz)
      tone(speakerpin, pitch, 3);  //plays a given tone for 2ms

    }
    for (int pitch = highpitch; pitch > lowpitch; pitch--) { // cycles the pitch down from higpitch to lowpitch
      // play the tone for 20 ms on pin 8
      tone(speakerpin, pitch, 3);

    }
  

  //delay(500);
  digitalWrite(4, LOW);

}
